// Logisim project Fetch-execute.circ as structural Verilog: 1 circuit, main circuit main
module main (
  input  _1,
  input  _0,
  output execute,
  output fetch
);

  wire clock_out;
  wire [15:0] adder_1_out, PC_q, ram_1_data;

  Clock clock (.out(clock_out));
  Counter #(.width(1), .max('h1)) counter (.Q(fetch), .clk(clock_out));  // open: load, D, count, carry, clr
  not not_1 (execute, fetch);
  Adder #(.width(16)) adder_1 (.a(PC_q), .b(16'h1), .out(adder_1_out));  // open: cin, cout
  Register #(.width(16)) PC (.D(adder_1_out), .Q(PC_q), .clk(execute));  // open: en, clr
  RAM #(.addrWidth(16), .dataWidth(16)) ram_1 (.addr(PC_q), .data(ram_1_data), .clk(fetch));  // open: sel, ld, clr
  Register #(.width(16), .trigger("high")) IR (.D(ram_1_data), .clk(fetch));  // open: en, Q, clr
endmodule
